# Fritzing sketch diagram (saved by Fritzing 0.9.3b)
breadboards: 1

parts:
  Arduino_Pro_Mini_5V = Arduino Pro Mini (5V)
  OLED_I2C1 = OLED 128x64 I2C Monochrome Display
  30N60 = NPN-Transistor [package="TO92 [THT]"]
  DS1 = DS18B20 1-Wire Temperature Sensor [part_number=DS18B20]
  R1 = Resistor [tolerance=±5% resistance=1k package=THT]
  R2 = Resistor [tolerance=±5% resistance=3.3k package=THT]
  Load_Resistor = Resistor [tolerance=±5% resistance=2.5 power=50W package=THT]
  R3 = Resistor [tolerance=±5% resistance=4.7k package=THT]
  IC1 = Voltage Regulator [package=to220-igo]
  C1 = Electrolytic Capacitor [capacitance=10µF package="100 mil [THT, electrolytic]"]

nets:
  VCC: Arduino_Pro_Mini_5V.VCC, OLED_I2C1.VDD, IC1.OUT, C1.+
  Discharge -/GND: Arduino_Pro_Mini_5V.GND, OLED_I2C1.GND, 30N60.E, DS1.GND, R1.Pin_0, IC1.GND, C1.-
  N1: Arduino_Pro_Mini_5V.A4, OLED_I2C1.SDA
  N2: Arduino_Pro_Mini_5V.A5, OLED_I2C1.SCL
  N3: Arduino_Pro_Mini_5V.A0, R1.Pin_1, R2.Pin_0
  N4: Arduino_Pro_Mini_5V.D10, 30N60.B
  N5: Arduino_Pro_Mini_5V.D2, DS1.DQ, R3.Pin_1
  N6: 30N60.C, Load_Resistor.Pin_0
  N7: DS1.VDD, R3.Pin_0
  Discharge +: R2.Pin_1, Load_Resistor.Pin_1
  12V: IC1.IN
